// Logisim project 8-bit-cpu-circ.circ as structural Verilog: 1 circuit, main circuit main
module main (
  input  [3:0] in_1,
  input  [7:0] in_2,
  input  in_3,
  output [7:0] Bus,
  output [7:0] out_5,
  output [6:0] out_6
);

  wire AI, and_2_out, AO, BI, CE, CLK, clock_1_out, CLR, CO, EO, HLT, II, IO, J, MI, multiplexer_1_out,
       not_1_out, not_2_out, OI, or_1_out, RAM_PROG_LOAD, RI, RO, SU;
  wire [3:0] ADD_REG_O, counter_1_q, INST_REG_O, multiplexer_2_out;
  wire [7:0] adder_1_out, ALU_AI, ALU_BI, multiplexer_3_out, OO, xor_1_out;
  wire [15:15] instructions_data;

  Clock clock_1 (.out(clock_1_out));
  and and_1 (CLK, ~HLT, clock_1_out);  // AND_Gate
  Register register_1 (.D(Bus), .en(BI), .clk(CLK), .Q(ALU_BI), .clr(CLR));
  Register register_2 (.D(Bus), .en(AI), .clk(CLK), .Q(ALU_AI), .clr(CLR));
  assign xor_1_out = {8{SU}} ^ ALU_BI;  // XOR_Gate xor_1, 8 bits wide
  assign Bus = AO ? ALU_AI : 8'bz;  // Controlled_Buffer controlled_buffer_1
  assign Bus = EO ? adder_1_out : 8'bz;  // Controlled_Buffer controlled_buffer_2
  Adder adder_1 (.a(ALU_AI), .b(xor_1_out), .out(adder_1_out), .cin(SU));  // open: cout
  ROM #(.addrWidth(7), .dataWidth(16)) instructions (
    .addr(out_6), .data({instructions_data[15], HLT, MI, RI, RO, IO, II, AI, AO, EO, SU, BI, OI, CE, CO, J}));
  Register register_3 (.D(Bus), .en(II), .clk(CLK), .Q({out_6[6:3], INST_REG_O}), .clr(CLR));
  or or_1 (or_1_out, J, CE);
  assign Bus = IO ? {out_6[6:3], INST_REG_O} : 8'bz;  // Controlled_Buffer controlled_buffer_3
  Button button_1 (.out(CLR));
  not not_1 (not_1_out, J);
  and and_2 (and_2_out, or_1_out, CLK);
  Counter #(.max('hf), .width(4)) counter_1 (
    .clr(CLR), .load(J), .count(not_1_out), .clk(and_2_out), .D(Bus[3:0]), .Q(counter_1_q));  // open: up, carry
  Hex_Digit_Display hex_digit_display_1 (.value(OO[7:4]));  // open: dp
  Hex_Digit_Display hex_digit_display_2 (.value(OO[3:0]));  // open: dp
  Button button_2 (.out(RAM_PROG_LOAD));
  Register #(.width(4)) register_4 (.D(Bus[3:0]), .en(MI), .clk(CLK), .Q(ADD_REG_O), .clr(CLR));
  assign Bus = CO ? {4'b0000, counter_1_q} : 8'bz;  // Controlled_Buffer controlled_buffer_4
  Counter #(.max('h7), .width(3)) counter_2 (
    .clr(CLR), .clk(not_2_out), .Q(out_6[2:0]));  // open: load, up, count, D, carry
  not not_2 (not_2_out, CLK);
  Register register_5 (.D(Bus), .en(OI), .clk(CLK), .Q(OO), .clr(CLR));
  Multiplexer #(.enable("true")) multiplexer_1 (
    .in0(RAM_PROG_LOAD), .in1(RI), .out(multiplexer_1_out), .sel(in_3));  // open: en
  Multiplexer #(.enable("true"), .width(4)) multiplexer_2 (
    .in0(in_1), .in1(ADD_REG_O), .out(multiplexer_2_out), .sel(in_3));  // open: en
  Multiplexer #(.enable("true"), .width(8)) multiplexer_3 (
    .in0(in_2), .in1(Bus), .out(multiplexer_3_out), .sel(in_3));  // open: en
  RAM #(.addrWidth(4), .enables("line")) ram_1 (
    .addr(multiplexer_2_out), .we(multiplexer_1_out), .clk(CLK), .din(multiplexer_3_out), .dout(out_5));
  assign Bus = RO ? out_5 : 8'bz;  // Controlled_Buffer controlled_buffer_5

  // Other names for the same wires on the sheet: ADD_PROG_INPUT[3:0] = in_1; MICRO_INST_COUNTER_O[2:0] = out_6[2:0];
  //   INST_REG_O[7:4] = out_6[6:3]; RAM_PROG_INPUT[7:0] = in_2; RUN_MODE = in_3

  // Notes on the sheet:
  //   A Reg
  //   B Reg
  //   ALU
  //   contents of instructions (hex, n*v repeats v):
  //   2002 a04 6*0 2002 a04 2400 900 4*0 2002 a04 2400 810 140 0 0 0 2002 a04 6*0 2002 a04 6*0 2002 a04
  //   6*0 2002 a04 6*0 2002 a04 6*0 2002 a04 6*0 2002 a04 6*0 2002 a04 6*0 2002 a04 6*0 2002 a04 6*0 2002
  //   a04 6*0 2002 a04 88 5*0 2002 a04 4000
  //   Instruction Reg
  //   Display
  //   Input
  //   Program Counter
  //   Address Reg
  //   Output Reg
  //   Control Logic
  //   Micro Instruction Counter
  //   ro turns on, memory is still outputting last data. ai turns on which causes reg a to get data from bus, but ram hasnt output new data yet.
  //   RAM
endmodule
